// Logisim project stage1.circ as structural Verilog: 2 circuits, main circuit calculator
module calculator (
  input  in_1,
  input  in_2,
  input  in_3,
  input  in_4,
  input  in_5,
  input  in_6,
  input  in_7,
  input  in_8,
  input  in_9,
  input  in_10,
  input  in_11,
  input  Input_B,
  input  in_13,
  input  in_14,
  input  in_15,
  input  in_16
);

  wire button_1_out, button_4_out;
  wire [7:0] load_reset_1_out_bit, load_reset_2_out_bit;

  Button button_1 (.out(button_1_out));
  Button button_2 ();  // open: out
  Button button_3 ();  // open: out
  Button button_4 (.out(button_4_out));
  Button button_5 ();  // open: out
  LED led_1 ();  // open: in
  LED led_2 (.in(load_reset_1_out_bit[7]));
  LED led_3 (.in(load_reset_1_out_bit[6]));
  LED led_4 (.in(load_reset_1_out_bit[5]));
  LED led_5 (.in(load_reset_1_out_bit[4]));
  LED led_6 (.in(load_reset_1_out_bit[3]));
  LED led_7 (.in(load_reset_1_out_bit[2]));
  LED led_8 ();  // open: in
  Load_Reset load_reset_1 (
    .in_bit({in_1, in_2, in_3, in_4, in_5, in_6, in_7, in_8}), .Load(button_1_out), .Reset(button_4_out),
    .out_bit(load_reset_1_out_bit));
  LED led_9 (.in(load_reset_1_out_bit[1]));
  LED led_10 ();  // open: in
  LED led_11 (.in(load_reset_1_out_bit[0]));
  LED led_12 ();  // open: in
  LED led_13 ();  // open: in
  LED led_14 ();  // open: in
  Button button_6 ();  // open: out
  LED led_15 ();  // open: in
  LED led_16 ();  // open: in
  LED led_17 ();  // open: in
  LED led_18 (.in(load_reset_2_out_bit[6]));
  LED led_19 (.in(load_reset_2_out_bit[7]));
  LED led_20 ();  // open: in
  LED led_21 ();  // open: in
  LED led_22 (.in(load_reset_2_out_bit[5]));
  LED led_23 (.in(load_reset_2_out_bit[4]));
  LED led_24 (.in(load_reset_2_out_bit[3]));
  Load_Reset load_reset_2 (
    .in_bit({in_9, in_10, in_11, Input_B, in_13, in_14, in_15, in_16}), .Load(button_1_out),
    .Reset(button_4_out), .out_bit(load_reset_2_out_bit));
  LED led_25 (.in(load_reset_2_out_bit[2]));
  LED led_26 (.in(load_reset_2_out_bit[1]));
  LED led_27 (.in(load_reset_2_out_bit[0]));

  // Notes on the sheet:
  //   Load
  //   Add
  //   Subtract
  //   Reset
  //   +/-
  //   +/-
  //   Input A
  //   Input A Display
  //   +/-
  //   8 bit Binary Calculator
  //   +/-
  //   +/-
  //   Output
  //   Input B Display
endmodule

module Load_Reset (
  input  [7:0] in_bit,
  input  Load,
  input  Reset,
  output [7:0] out_bit
);

  D_Flip_Flop d_ff_1 (.D(in_bit[0]), .clk(Load), .Q(out_bit[0]), .reset(Reset));  // open: Qn, preset
  D_Flip_Flop d_ff_2 (.D(in_bit[1]), .clk(Load), .Q(out_bit[1]), .reset(Reset));  // open: Qn, preset
  D_Flip_Flop d_ff_3 (.D(in_bit[2]), .clk(Load), .Q(out_bit[2]), .reset(Reset));  // open: Qn, preset
  D_Flip_Flop d_ff_4 (.D(in_bit[3]), .clk(Load), .Q(out_bit[3]), .reset(Reset));  // open: Qn, preset
  D_Flip_Flop d_ff_5 (.D(in_bit[4]), .clk(Load), .Q(out_bit[4]), .reset(Reset));  // open: Qn, preset
  D_Flip_Flop d_ff_6 (.D(in_bit[5]), .clk(Load), .Q(out_bit[5]), .reset(Reset));  // open: Qn, preset
  D_Flip_Flop d_ff_7 (.D(in_bit[6]), .clk(Load), .Q(out_bit[6]), .reset(Reset));  // open: Qn, preset
  D_Flip_Flop d_ff_8 (.D(in_bit[7]), .clk(Load), .Q(out_bit[7]), .reset(Reset));  // open: Qn, preset
endmodule
