// Logisim project stage2.circ as structural Verilog: 3 circuits, main circuit calculator
module calculator (
  input  in_1,
  input  in_2,
  input  in_3,
  input  in_4,
  input  in_5,
  input  in_6,
  input  in_7,
  input  in_8,
  input  in_9,
  input  in_10,
  input  in_11,
  input  Input_B,
  input  in_13,
  input  in_14,
  input  in_15,
  input  in_16
);

  wire button_1_out, button_2_out, button_4_out;
  wire [7:0] add_1_out_bit, load_reset_1_out_bit, load_reset_2_out_bit;

  Button button_1 (.out(button_1_out));
  Button button_2 (.out(button_2_out));
  Button button_3 ();  // open: out
  Button button_4 (.out(button_4_out));
  Button button_5 ();  // open: out
  LED led_1 ();  // open: in
  LED led_2 (.in(load_reset_1_out_bit[7]));
  LED led_3 (.in(load_reset_1_out_bit[6]));
  LED led_4 (.in(load_reset_1_out_bit[5]));
  LED led_5 (.in(load_reset_1_out_bit[4]));
  LED led_6 (.in(load_reset_1_out_bit[3]));
  LED led_7 (.in(load_reset_1_out_bit[2]));
  Load_Reset load_reset_1 (
    .in_bit({in_1, in_2, in_3, in_4, in_5, in_6, in_7, in_8}), .Load(button_1_out), .Reset(button_4_out),
    .out_bit(load_reset_1_out_bit));
  LED led_8 (.in(load_reset_1_out_bit[1]));
  LED led_9 ();  // open: in
  LED led_10 (.in(load_reset_1_out_bit[0]));
  LED led_11 (.in(add_1_out_bit[7]));
  LED led_12 (.in(add_1_out_bit[6]));
  LED led_13 (.in(add_1_out_bit[5]));
  Button button_6 ();  // open: out
  LED led_14 ();  // open: in
  LED led_15 (.in(add_1_out_bit[4]));
  LED led_16 (.in(add_1_out_bit[3]));
  LED led_17 (.in(load_reset_2_out_bit[6]));
  LED led_18 (.in(load_reset_2_out_bit[7]));
  Add add_1 (
    .A_in(load_reset_1_out_bit), .B_in(load_reset_2_out_bit), .Addition(button_2_out), .out_bit(add_1_out_bit));
  LED led_19 (.in(add_1_out_bit[2]));
  LED led_20 (.in(load_reset_2_out_bit[5]));
  LED led_21 (.in(add_1_out_bit[1]));
  LED led_22 (.in(add_1_out_bit[0]));
  LED led_23 (.in(load_reset_2_out_bit[4]));
  LED led_24 (.in(load_reset_2_out_bit[3]));
  Load_Reset load_reset_2 (
    .in_bit({in_9, in_10, in_11, Input_B, in_13, in_14, in_15, in_16}), .Load(button_1_out),
    .Reset(button_4_out), .out_bit(load_reset_2_out_bit));
  LED led_25 (.in(load_reset_2_out_bit[2]));
  LED led_26 (.in(load_reset_2_out_bit[1]));
  LED led_27 (.in(load_reset_2_out_bit[0]));

  // Notes on the sheet:
  //   Load
  //   Add
  //   Subtract
  //   Reset
  //   +/-
  //   +/-
  //   Input A
  //   Input A Display
  //   +/-
  //   8 bit Binary Calculator
  //   +/-
  //   +/-
  //   Output
  //   Input B Display
endmodule

module Load_Reset (
  input  [7:0] in_bit,
  input  Load,
  input  Reset,
  output [7:0] out_bit
);

  D_Flip_Flop d_ff_1 (.D(in_bit[0]), .clk(Load), .Q(out_bit[0]), .reset(Reset));  // open: Qn, preset
  D_Flip_Flop d_ff_2 (.D(in_bit[1]), .clk(Load), .Q(out_bit[1]), .reset(Reset));  // open: Qn, preset
  D_Flip_Flop d_ff_3 (.D(in_bit[2]), .clk(Load), .Q(out_bit[2]), .reset(Reset));  // open: Qn, preset
  D_Flip_Flop d_ff_4 (.D(in_bit[3]), .clk(Load), .Q(out_bit[3]), .reset(Reset));  // open: Qn, preset
  D_Flip_Flop d_ff_5 (.D(in_bit[4]), .clk(Load), .Q(out_bit[4]), .reset(Reset));  // open: Qn, preset
  D_Flip_Flop d_ff_6 (.D(in_bit[5]), .clk(Load), .Q(out_bit[5]), .reset(Reset));  // open: Qn, preset
  D_Flip_Flop d_ff_7 (.D(in_bit[6]), .clk(Load), .Q(out_bit[6]), .reset(Reset));  // open: Qn, preset
  D_Flip_Flop d_ff_8 (.D(in_bit[7]), .clk(Load), .Q(out_bit[7]), .reset(Reset));  // open: Qn, preset
endmodule

module Add (
  input  [7:0] A_in,
  input  [7:0] B_in,
  input  Addition,
  output [7:0] out_bit
);

  wire and_1_out, and_2_out, and_3_out, and_4_out, and_5_out, and_6_out, and_7_out, and_8_out, and_9_out,
       and_10_out, and_11_out, and_12_out, and_13_out, and_14_out, and_15_out, or_1_out, or_2_out, or_3_out,
       or_4_out, or_5_out, or_6_out, or_7_out, xor_1_out, xor_2_out, xor_3_out, xor_4_out, xor_5_out,
       xor_6_out, xor_7_out, xor_8_out, xor_9_out, xor_10_out, xor_11_out, xor_12_out, xor_13_out,
       xor_14_out, xor_15_out;

  xor xor_1 (xor_1_out, A_in[0], B_in[0]);
  and and_1 (and_1_out, A_in[0], B_in[0]);
  xor xor_2 (xor_2_out, A_in[1], B_in[1]);
  and and_2 (and_2_out, A_in[1], B_in[1]);
  xor xor_3 (xor_3_out, A_in[2], B_in[2]);
  and and_3 (and_3_out, A_in[2], B_in[2]);
  xor xor_4 (xor_4_out, A_in[3], B_in[3]);
  and and_4 (and_4_out, A_in[3], B_in[3]);
  xor xor_5 (xor_5_out, A_in[4], B_in[4]);
  and and_5 (and_5_out, A_in[4], B_in[4]);
  xor xor_6 (xor_6_out, A_in[5], B_in[5]);
  and and_6 (and_6_out, A_in[5], B_in[5]);
  xor xor_7 (xor_7_out, A_in[6], B_in[6]);
  and and_7 (and_7_out, A_in[6], B_in[6]);
  xor xor_8 (xor_8_out, A_in[7], B_in[7]);
  and and_8 (and_8_out, A_in[7], B_in[7]);
  xor xor_9 (xor_9_out, and_1_out, xor_2_out);
  and and_9 (and_9_out, and_1_out, xor_2_out);
  xor xor_10 (xor_10_out, or_1_out, xor_3_out);
  and and_10 (and_10_out, or_1_out, xor_3_out);
  xor xor_11 (xor_11_out, or_2_out, xor_4_out);
  and and_11 (and_11_out, or_2_out, xor_4_out);
  xor xor_12 (xor_12_out, or_3_out, xor_5_out);
  and and_12 (and_12_out, or_3_out, xor_5_out);
  xor xor_13 (xor_13_out, or_4_out, xor_6_out);
  and and_13 (and_13_out, or_4_out, xor_6_out);
  xor xor_14 (xor_14_out, or_5_out, xor_7_out);
  and and_14 (and_14_out, or_5_out, xor_7_out);
  xor xor_15 (xor_15_out, or_6_out, xor_8_out);
  and and_15 (and_15_out, or_6_out, xor_8_out);
  or or_1 (or_1_out, and_9_out, and_2_out);
  or or_2 (or_2_out, and_10_out, and_3_out);
  or or_3 (or_3_out, and_11_out, and_4_out);
  or or_4 (or_4_out, and_12_out, and_5_out);
  or or_5 (or_5_out, and_13_out, and_6_out);
  or or_6 (or_6_out, and_14_out, and_7_out);
  or or_7 (or_7_out, and_15_out, and_8_out);
  D_Flip_Flop d_ff_1 (.D(xor_1_out), .clk(Addition), .Q(out_bit[0]));  // open: Qn, preset, reset
  D_Flip_Flop d_ff_2 (.D(xor_9_out), .clk(Addition), .Q(out_bit[1]));  // open: Qn, preset, reset
  D_Flip_Flop d_ff_3 (.D(xor_10_out), .clk(Addition), .Q(out_bit[2]));  // open: Qn, preset, reset
  D_Flip_Flop d_ff_4 (.D(xor_11_out), .clk(Addition), .Q(out_bit[3]));  // open: Qn, preset, reset
  D_Flip_Flop d_ff_5 (.D(xor_12_out), .clk(Addition), .Q(out_bit[4]));  // open: Qn, preset, reset
  D_Flip_Flop d_ff_6 (.D(xor_13_out), .clk(Addition), .Q(out_bit[5]));  // open: Qn, preset, reset
  D_Flip_Flop d_ff_7 (.D(xor_14_out), .clk(Addition), .Q(out_bit[6]));  // open: Qn, preset, reset
  D_Flip_Flop d_ff_8 (.D(xor_15_out), .Q(out_bit[7]));  // open: clk, Qn, preset, reset
  LED led_1 (.in(or_7_out));
endmodule
