// Logisim project stage4.circ as structural Verilog: 12 circuits, main circuit calculator
module calculator (
  input  in_1,
  input  in_2,
  input  in_3,
  input  in_4,
  input  in_5,
  input  in_6,
  input  in_7,
  input  in_8,
  input  in_9,
  input  in_10,
  input  in_11,
  input  Input_B,
  input  in_13,
  input  in_14,
  input  in_15,
  input  in_16
);

  wire button_1_out, button_2_out, button_3_out, button_4_out, button_5_out, button_6_out,
       stage3_complement_2s_1_outpm, stage3_complement_2s_2_outpm, stage4_calculate_1_outswitch;
  wire [7:0] stage1_load_reset_1_out_bit, stage1_load_reset_2_out_bit, stage3_complement_2s_1_out_bit,
       stage3_complement_2s_2_out_bit, stage4_calculate_1_out_bit;

  Button button_1 (.out(button_1_out));
  Button button_2 (.out(button_2_out));
  Button button_3 (.out(button_3_out));
  Button button_4 (.out(button_4_out));
  Button button_5 (.out(button_5_out));
  LED led_1 (.in(stage3_complement_2s_1_outpm));
  LED led_2 (.in(stage3_complement_2s_1_out_bit[7]));
  LED led_3 (.in(stage3_complement_2s_1_out_bit[6]));
  LED led_4 (.in(stage3_complement_2s_1_out_bit[5]));
  LED led_5 (.in(stage3_complement_2s_1_out_bit[4]));
  LED led_6 (.in(stage4_calculate_1_outswitch));
  LED led_7 (.in(stage3_complement_2s_1_out_bit[3]));
  LED led_8 (.in(stage3_complement_2s_1_out_bit[2]));
  LED led_9 (.in(stage4_calculate_1_out_bit[7]));
  Stage1_Load_Reset stage1_load_reset_1 (
    .in_bit({in_1, in_2, in_3, in_4, in_5, in_6, in_7, in_8}), .Load(button_1_out), .Reset(button_4_out),
    .out_bit(stage1_load_reset_1_out_bit));
  Stage3_Complement_2s stage3_complement_2s_1 (
    .in_bit(stage1_load_reset_1_out_bit), .Switch(button_5_out), .out_bit(stage3_complement_2s_1_out_bit),
    .outPM(stage3_complement_2s_1_outpm));
  LED led_10 (.in(stage3_complement_2s_1_out_bit[1]));
  LED led_11 (.in(stage4_calculate_1_out_bit[6]));
  LED led_12 (.in(stage4_calculate_1_out_bit[5]));
  LED led_13 (.in(stage3_complement_2s_1_out_bit[0]));
  LED led_14 (.in(stage4_calculate_1_out_bit[4]));
  LED led_15 (.in(stage4_calculate_1_out_bit[2]));
  LED led_16 (.in(stage4_calculate_1_out_bit[3]));
  Button button_6 (.out(button_6_out));
  LED led_17 (.in(stage3_complement_2s_2_outpm));
  Stage4_calculate stage4_calculate_1 (
    .A_in(stage3_complement_2s_1_out_bit), .B_in(stage3_complement_2s_2_out_bit), .Add(button_2_out),
    .Subtract(button_3_out), .out_bit(stage4_calculate_1_out_bit), .outSwitch(stage4_calculate_1_outswitch));
  LED led_18 (.in(stage4_calculate_1_out_bit[1]));
  LED led_19 (.in(stage4_calculate_1_out_bit[0]));
  LED led_20 (.in(stage3_complement_2s_2_out_bit[7]));
  LED led_21 (.in(stage3_complement_2s_2_out_bit[6]));
  LED led_22 (.in(stage3_complement_2s_2_out_bit[5]));
  LED led_23 (.in(stage3_complement_2s_2_out_bit[4]));
  LED led_24 (.in(stage3_complement_2s_2_out_bit[3]));
  Stage1_Load_Reset stage1_load_reset_2 (
    .in_bit({in_9, in_10, in_11, Input_B, in_13, in_14, in_15, in_16}), .Load(button_1_out),
    .Reset(button_4_out), .out_bit(stage1_load_reset_2_out_bit));
  Stage3_Complement_2s stage3_complement_2s_2 (
    .in_bit(stage1_load_reset_2_out_bit), .Switch(button_6_out), .out_bit(stage3_complement_2s_2_out_bit),
    .outPM(stage3_complement_2s_2_outpm));
  LED led_25 (.in(stage3_complement_2s_2_out_bit[2]));
  LED led_26 (.in(stage3_complement_2s_2_out_bit[1]));
  LED led_27 (.in(stage3_complement_2s_2_out_bit[0]));

  // Notes on the sheet:
  //   Load
  //   Add
  //   Subtract
  //   Reset
  //   +/-
  //   +/-
  //   Input A
  //   Input A Display
  //   +/-
  //   8 bit Binary Calculator
  //   Output
  //   the output will be displayed as unsigned number, with led to know if it's positive or negative
  //   +/-
  //   +/-
  //   Input B Display
endmodule

module Stage1_Load_Reset (
  input  [7:0] in_bit,
  input  Load,
  input  Reset,
  output [7:0] out_bit
);

  D_Flip_Flop d_ff_1 (.D(in_bit[0]), .clk(Load), .Q(out_bit[0]), .reset(Reset));  // open: Qn, preset
  D_Flip_Flop d_ff_2 (.D(in_bit[1]), .clk(Load), .Q(out_bit[1]), .reset(Reset));  // open: Qn, preset
  D_Flip_Flop d_ff_3 (.D(in_bit[2]), .clk(Load), .Q(out_bit[2]), .reset(Reset));  // open: Qn, preset
  D_Flip_Flop d_ff_4 (.D(in_bit[3]), .clk(Load), .Q(out_bit[3]), .reset(Reset));  // open: Qn, preset
  D_Flip_Flop d_ff_5 (.D(in_bit[4]), .clk(Load), .Q(out_bit[4]), .reset(Reset));  // open: Qn, preset
  D_Flip_Flop d_ff_6 (.D(in_bit[5]), .clk(Load), .Q(out_bit[5]), .reset(Reset));  // open: Qn, preset
  D_Flip_Flop d_ff_7 (.D(in_bit[6]), .clk(Load), .Q(out_bit[6]), .reset(Reset));  // open: Qn, preset
  D_Flip_Flop d_ff_8 (.D(in_bit[7]), .clk(Load), .Q(out_bit[7]), .reset(Reset));  // open: Qn, preset
endmodule

module Stage2_Add (
  input  [7:0] A_in,
  input  [7:0] B_in,
  input  Button,
  output [7:0] out_bit
);

  wire and_1_out, and_2_out, and_3_out, and_4_out, and_5_out, and_6_out, and_7_out, and_8_out, and_9_out,
       and_10_out, and_11_out, and_12_out, and_13_out, and_14_out, and_15_out, or_1_out, or_2_out, or_3_out,
       or_4_out, or_5_out, or_6_out, or_7_out, xor_1_out, xor_2_out, xor_3_out, xor_4_out, xor_5_out,
       xor_6_out, xor_7_out, xor_8_out, xor_9_out, xor_10_out, xor_11_out, xor_12_out, xor_13_out,
       xor_14_out, xor_15_out;

  xor xor_1 (xor_1_out, A_in[0], B_in[0]);
  and and_1 (and_1_out, A_in[0], B_in[0]);
  xor xor_2 (xor_2_out, A_in[1], B_in[1]);
  and and_2 (and_2_out, A_in[1], B_in[1]);
  xor xor_3 (xor_3_out, A_in[2], B_in[2]);
  and and_3 (and_3_out, A_in[2], B_in[2]);
  xor xor_4 (xor_4_out, A_in[3], B_in[3]);
  and and_4 (and_4_out, A_in[3], B_in[3]);
  xor xor_5 (xor_5_out, A_in[4], B_in[4]);
  and and_5 (and_5_out, A_in[4], B_in[4]);
  xor xor_6 (xor_6_out, A_in[5], B_in[5]);
  and and_6 (and_6_out, A_in[5], B_in[5]);
  xor xor_7 (xor_7_out, A_in[6], B_in[6]);
  and and_7 (and_7_out, A_in[6], B_in[6]);
  xor xor_8 (xor_8_out, A_in[7], B_in[7]);
  and and_8 (and_8_out, A_in[7], B_in[7]);
  xor xor_9 (xor_9_out, and_1_out, xor_2_out);
  and and_9 (and_9_out, and_1_out, xor_2_out);
  xor xor_10 (xor_10_out, or_1_out, xor_3_out);
  and and_10 (and_10_out, or_1_out, xor_3_out);
  xor xor_11 (xor_11_out, or_2_out, xor_4_out);
  and and_11 (and_11_out, or_2_out, xor_4_out);
  xor xor_12 (xor_12_out, or_3_out, xor_5_out);
  and and_12 (and_12_out, or_3_out, xor_5_out);
  xor xor_13 (xor_13_out, or_4_out, xor_6_out);
  and and_13 (and_13_out, or_4_out, xor_6_out);
  xor xor_14 (xor_14_out, or_5_out, xor_7_out);
  and and_14 (and_14_out, or_5_out, xor_7_out);
  xor xor_15 (xor_15_out, or_6_out, xor_8_out);
  and and_15 (and_15_out, or_6_out, xor_8_out);
  or or_1 (or_1_out, and_9_out, and_2_out);
  or or_2 (or_2_out, and_10_out, and_3_out);
  or or_3 (or_3_out, and_11_out, and_4_out);
  or or_4 (or_4_out, and_12_out, and_5_out);
  or or_5 (or_5_out, and_13_out, and_6_out);
  or or_6 (or_6_out, and_14_out, and_7_out);
  or or_7 (or_7_out, and_15_out, and_8_out);
  D_Flip_Flop d_ff_1 (.D(xor_1_out), .clk(Button), .Q(out_bit[0]));  // open: Qn, preset, reset
  D_Flip_Flop d_ff_2 (.D(xor_9_out), .clk(Button), .Q(out_bit[1]));  // open: Qn, preset, reset
  D_Flip_Flop d_ff_3 (.D(xor_10_out), .clk(Button), .Q(out_bit[2]));  // open: Qn, preset, reset
  D_Flip_Flop d_ff_4 (.D(xor_11_out), .clk(Button), .Q(out_bit[3]));  // open: Qn, preset, reset
  D_Flip_Flop d_ff_5 (.D(xor_12_out), .clk(Button), .Q(out_bit[4]));  // open: Qn, preset, reset
  D_Flip_Flop d_ff_6 (.D(xor_13_out), .clk(Button), .Q(out_bit[5]));  // open: Qn, preset, reset
  D_Flip_Flop d_ff_7 (.D(xor_14_out), .clk(Button), .Q(out_bit[6]));  // open: Qn, preset, reset
  D_Flip_Flop d_ff_8 (.D(xor_15_out), .clk(Button), .Q(out_bit[7]));  // open: Qn, preset, reset
  LED led_1 (.in(or_7_out));
endmodule

module Stage3_Complement_2s (
  input  [7:0] in_bit,
  input  Switch,
  output [7:0] out_bit,
  output outPM
);

  wire and_1_out, and_2_out, and_3_out, and_4_out, and_5_out, and_6_out, and_7_out, and_8_out, not_1_out,
       not_2_out, not_3_out, not_4_out, not_5_out, not_6_out, not_7_out, not_8_out, t_ff_1_q;
  wire [7:0] xor_1_out;

  not not_1 (not_1_out, in_bit[0]);
  not not_2 (not_2_out, in_bit[1]);
  not not_3 (not_3_out, in_bit[2]);
  not not_4 (not_4_out, in_bit[3]);
  not not_5 (not_5_out, in_bit[4]);
  not not_6 (not_6_out, in_bit[5]);
  not not_7 (not_7_out, in_bit[6]);
  not not_8 (not_8_out, in_bit[7]);
  xor xor_1 (xor_1_out[0], 1'b1, not_1_out);
  and and_1 (and_1_out, 1'b1, not_1_out);
  xor xor_2 (xor_1_out[1], and_1_out, not_2_out);
  and and_2 (and_2_out, and_1_out, not_2_out);
  xor xor_3 (xor_1_out[2], and_2_out, not_3_out);
  and and_3 (and_3_out, and_2_out, not_3_out);
  xor xor_4 (xor_1_out[3], and_3_out, not_4_out);
  and and_4 (and_4_out, and_3_out, not_4_out);
  xor xor_5 (xor_1_out[4], and_4_out, not_5_out);
  and and_5 (and_5_out, and_4_out, not_5_out);
  xor xor_6 (xor_1_out[5], and_5_out, not_6_out);
  and and_6 (and_6_out, and_5_out, not_6_out);
  xor xor_7 (xor_1_out[6], and_6_out, not_7_out);
  and and_7 (and_7_out, and_6_out, not_7_out);
  xor xor_8 (xor_1_out[7], and_7_out, not_8_out);
  and and_8 (and_8_out, and_7_out, not_8_out);
  LED led_1 (.in(and_8_out));
  T_Flip_Flop t_ff_1 (.T(Switch), .clk(Switch), .Q(t_ff_1_q));  // open: Qn, reset, preset
  Stage3_Multiplexer stage3_multiplexer_1 (
    .option0(in_bit), .option1(xor_1_out), .inPlusMinus(t_ff_1_q), .out_bit(out_bit), .outPlusMinus(outPM));
endmodule

module Stage3_Multiplexer (
  input  [7:0] option0,
  input  [7:0] option1,
  input  inPlusMinus,
  output [7:0] out_bit,
  output outPlusMinus
);

  wire and_1_out, and_2_out, and_3_out, and_4_out, and_5_out, and_6_out, and_7_out, and_8_out, and_9_out,
       and_10_out, and_11_out, and_12_out, and_13_out, and_14_out, and_15_out, and_16_out, not_1_out,
       not_2_out, not_3_out, not_4_out, not_5_out, not_6_out, not_7_out, not_8_out;

  not not_1 (not_1_out, inPlusMinus);
  not not_2 (not_2_out, inPlusMinus);
  not not_3 (not_3_out, inPlusMinus);
  not not_4 (not_4_out, inPlusMinus);
  not not_5 (not_5_out, inPlusMinus);
  not not_6 (not_6_out, inPlusMinus);
  not not_7 (not_7_out, inPlusMinus);
  not not_8 (not_8_out, inPlusMinus);
  and and_1 (and_1_out, option0[0], not_1_out);
  and and_2 (and_2_out, option1[0], inPlusMinus);
  and and_3 (and_3_out, option0[1], not_2_out);
  and and_4 (and_4_out, option1[1], inPlusMinus);
  and and_5 (and_5_out, option0[2], not_3_out);
  and and_6 (and_6_out, option1[2], inPlusMinus);
  and and_7 (and_7_out, option0[3], not_4_out);
  and and_8 (and_8_out, option1[3], inPlusMinus);
  and and_9 (and_9_out, option0[4], not_5_out);
  and and_10 (and_10_out, option1[4], inPlusMinus);
  and and_11 (and_11_out, option0[5], not_6_out);
  and and_12 (and_12_out, option1[5], inPlusMinus);
  and and_13 (and_13_out, option0[6], not_7_out);
  and and_14 (and_14_out, option1[6], inPlusMinus);
  and and_15 (and_15_out, option0[7], not_8_out);
  and and_16 (and_16_out, option1[7], inPlusMinus);
  or or_1 (out_bit[0], and_1_out, and_2_out);
  or or_2 (out_bit[1], and_3_out, and_4_out);
  or or_3 (out_bit[2], and_5_out, and_6_out);
  or or_4 (out_bit[3], and_7_out, and_8_out);
  or or_5 (out_bit[4], and_9_out, and_10_out);
  or or_6 (out_bit[5], and_11_out, and_12_out);
  or or_7 (out_bit[6], and_13_out, and_14_out);
  or or_8 (out_bit[7], and_15_out, and_16_out);

  assign outPlusMinus = inPlusMinus;
endmodule

module Stage4_2s_NegativeOnly (
  input  [7:0] in_bit,
  output [7:0] out_bit
);

  wire and_1_out, and_2_out, and_3_out, and_4_out, and_5_out, and_6_out, and_7_out, and_8_out, not_1_out,
       not_2_out, not_3_out, not_4_out, not_5_out, not_6_out, not_7_out, not_8_out;

  not not_1 (not_1_out, in_bit[0]);
  not not_2 (not_2_out, in_bit[1]);
  not not_3 (not_3_out, in_bit[2]);
  not not_4 (not_4_out, in_bit[3]);
  not not_5 (not_5_out, in_bit[4]);
  not not_6 (not_6_out, in_bit[5]);
  not not_7 (not_7_out, in_bit[6]);
  not not_8 (not_8_out, in_bit[7]);
  xor xor_1 (out_bit[0], 1'b1, not_1_out);
  and and_1 (and_1_out, 1'b1, not_1_out);
  xor xor_2 (out_bit[1], and_1_out, not_2_out);
  and and_2 (and_2_out, and_1_out, not_2_out);
  xor xor_3 (out_bit[2], and_2_out, not_3_out);
  and and_3 (and_3_out, and_2_out, not_3_out);
  xor xor_4 (out_bit[3], and_3_out, not_4_out);
  and and_4 (and_4_out, and_3_out, not_4_out);
  xor xor_5 (out_bit[4], and_4_out, not_5_out);
  and and_5 (and_5_out, and_4_out, not_5_out);
  xor xor_6 (out_bit[5], and_5_out, not_6_out);
  and and_6 (and_6_out, and_5_out, not_6_out);
  xor xor_7 (out_bit[6], and_6_out, not_7_out);
  and and_7 (and_7_out, and_6_out, not_7_out);
  xor xor_8 (out_bit[7], and_7_out, not_8_out);
  and and_8 (and_8_out, and_7_out, not_8_out);
  LED led_1 (.in(and_8_out));
endmodule

module Stage4_Subtraction (
  input  [7:0] A_in,
  input  [7:0] B_in,
  input  Subtract,
  output [7:0] out_bit
);

  wire [7:0] stage4_2s_negativeonly_1_out_bit;

  Stage4_2s_NegativeOnly stage4_2s_negativeonly_1 (.in_bit(B_in), .out_bit(stage4_2s_negativeonly_1_out_bit));
  Stage2_Add stage2_add_1 (.A_in(A_in), .B_in(stage4_2s_negativeonly_1_out_bit), .Button(Subtract), .out_bit(out_bit));
endmodule

module Stage4_calculate (
  input  [7:0] A_in,
  input  [7:0] B_in,
  input  Add,
  input  Subtract,
  output [7:0] out_bit,
  output outSwitch
);

  wire [7:0] stage2_add_1_out_bit, stage4_mux_1_out_bit, stage4_subtraction_1_out_bit;

  Stage2_Add stage2_add_1 (.A_in(A_in), .B_in(B_in), .Button(Add), .out_bit(stage2_add_1_out_bit));
  Stage4_Subtraction stage4_subtraction_1 (
    .A_in(A_in), .B_in(B_in), .Subtract(Subtract), .out_bit(stage4_subtraction_1_out_bit));
  Stage4_mux stage4_mux_1 (
    .Add_in(stage2_add_1_out_bit), .Subtract_in(stage4_subtraction_1_out_bit), .Add(Add),
    .Subtract(Subtract), .out_bit(stage4_mux_1_out_bit));
  Stage4_2stoUnsigned stage4_2stounsigned_1 (
    .in_bit(stage4_mux_1_out_bit), .inPlusMinus(stage4_mux_1_out_bit[7]), .out_bit(out_bit),
    .outPlusMinus(outSwitch));
endmodule

module Stage4_mux (
  input  [7:0] Add_in,
  input  [7:0] Subtract_in,
  input  Add,
  input  Subtract,
  output [7:0] out_bit
);

  wire and_1_out, and_2_out, and_3_out, and_4_out, and_5_out, and_6_out, and_7_out, and_8_out, and_9_out,
       and_10_out, and_11_out, and_12_out, and_13_out, and_14_out, and_15_out, and_16_out, and_17_out,
       d_ff_1_q, d_ff_2_q, not_1_out, not_2_out, not_3_out, not_4_out, not_5_out, not_6_out, not_7_out,
       not_8_out, not_9_out;

  D_Flip_Flop d_ff_1 (.D(Subtract), .clk(Subtract), .Q(d_ff_1_q), .reset(Add));  // open: Qn, preset
  D_Flip_Flop d_ff_2 (.D(Add), .clk(Add), .Q(d_ff_2_q), .reset(Subtract));  // open: Qn, preset
  not not_1 (not_1_out, d_ff_2_q);
  and and_1 (and_1_out, d_ff_1_q, not_1_out);
  not not_2 (not_2_out, and_1_out);
  not not_3 (not_3_out, and_1_out);
  not not_4 (not_4_out, and_1_out);
  not not_5 (not_5_out, and_1_out);
  not not_6 (not_6_out, and_1_out);
  not not_7 (not_7_out, and_1_out);
  not not_8 (not_8_out, and_1_out);
  not not_9 (not_9_out, and_1_out);
  and and_2 (and_2_out, Add_in[0], not_2_out);
  and and_3 (and_3_out, Subtract_in[0], and_1_out);
  and and_4 (and_4_out, Add_in[1], not_3_out);
  and and_5 (and_5_out, Subtract_in[1], and_1_out);
  and and_6 (and_6_out, Add_in[2], not_4_out);
  and and_7 (and_7_out, Subtract_in[2], and_1_out);
  and and_8 (and_8_out, Add_in[3], not_5_out);
  and and_9 (and_9_out, Subtract_in[3], and_1_out);
  and and_10 (and_10_out, Add_in[4], not_6_out);
  and and_11 (and_11_out, Subtract_in[4], and_1_out);
  and and_12 (and_12_out, Add_in[5], not_7_out);
  and and_13 (and_13_out, Subtract_in[5], and_1_out);
  and and_14 (and_14_out, Add_in[6], not_8_out);
  and and_15 (and_15_out, Subtract_in[6], and_1_out);
  and and_16 (and_16_out, Add_in[7], not_9_out);
  and and_17 (and_17_out, Subtract_in[7], and_1_out);
  or or_1 (out_bit[0], and_2_out, and_3_out);
  or or_2 (out_bit[1], and_4_out, and_5_out);
  or or_3 (out_bit[2], and_6_out, and_7_out);
  or or_4 (out_bit[3], and_8_out, and_9_out);
  or or_5 (out_bit[4], and_10_out, and_11_out);
  or or_6 (out_bit[5], and_12_out, and_13_out);
  or or_7 (out_bit[6], and_14_out, and_15_out);
  or or_8 (out_bit[7], and_16_out, and_17_out);
endmodule

module Stage4_2stoUnsigned (
  input  [7:0] in_bit,
  input  inPlusMinus,
  output [7:0] out_bit,
  output outPlusMinus
);

  wire [7:0] stage4_2sminus1_1_out_bit, stage4_flipdata_1_out_bit;

  Stage4_2sMinus1 stage4_2sminus1_1 (.in_bit(in_bit), .out_bit(stage4_2sminus1_1_out_bit));
  Stage4_FlipData stage4_flipdata_1 (.in_bit(stage4_2sminus1_1_out_bit), .out_bit(stage4_flipdata_1_out_bit));
  Stage3_Multiplexer stage3_multiplexer_1 (
    .option0(in_bit), .option1(stage4_flipdata_1_out_bit), .inPlusMinus(inPlusMinus), .out_bit(out_bit),
    .outPlusMinus(outPlusMinus));
endmodule

module Stage4_2sMinus1 (
  input  [7:0] in_bit,
  output [7:0] out_bit
);

  wire and_1_out, and_2_out, and_3_out, and_4_out, and_5_out, and_6_out, and_7_out, and_8_out, and_9_out,
       and_10_out, and_11_out, and_12_out, and_13_out, and_14_out, and_15_out, or_1_out, or_2_out, or_3_out,
       or_4_out, or_5_out, or_6_out, or_7_out, xor_2_out, xor_3_out, xor_4_out, xor_5_out, xor_6_out,
       xor_7_out, xor_8_out;

  xor xor_1 (out_bit[0], in_bit[0], 1'b1);
  and and_1 (and_1_out, in_bit[0], 1'b1);
  xor xor_2 (xor_2_out, in_bit[1], 1'b1);
  and and_2 (and_2_out, in_bit[1], 1'b1);
  xor xor_3 (xor_3_out, in_bit[2], 1'b1);
  and and_3 (and_3_out, in_bit[2], 1'b1);
  xor xor_4 (xor_4_out, in_bit[3], 1'b1);
  and and_4 (and_4_out, in_bit[3], 1'b1);
  xor xor_5 (xor_5_out, in_bit[4], 1'b1);
  and and_5 (and_5_out, in_bit[4], 1'b1);
  xor xor_6 (xor_6_out, in_bit[5], 1'b1);
  and and_6 (and_6_out, in_bit[5], 1'b1);
  xor xor_7 (xor_7_out, in_bit[6], 1'b1);
  and and_7 (and_7_out, in_bit[6], 1'b1);
  xor xor_8 (xor_8_out, in_bit[7], 1'b1);
  and and_8 (and_8_out, in_bit[7], 1'b1);
  xor xor_9 (out_bit[1], and_1_out, xor_2_out);
  and and_9 (and_9_out, and_1_out, xor_2_out);
  xor xor_10 (out_bit[2], or_1_out, xor_3_out);
  and and_10 (and_10_out, or_1_out, xor_3_out);
  xor xor_11 (out_bit[3], or_2_out, xor_4_out);
  and and_11 (and_11_out, or_2_out, xor_4_out);
  xor xor_12 (out_bit[4], or_3_out, xor_5_out);
  and and_12 (and_12_out, or_3_out, xor_5_out);
  xor xor_13 (out_bit[5], or_4_out, xor_6_out);
  and and_13 (and_13_out, or_4_out, xor_6_out);
  xor xor_14 (out_bit[6], or_5_out, xor_7_out);
  and and_14 (and_14_out, or_5_out, xor_7_out);
  xor xor_15 (out_bit[7], or_6_out, xor_8_out);
  and and_15 (and_15_out, or_6_out, xor_8_out);
  or or_1 (or_1_out, and_9_out, and_2_out);
  or or_2 (or_2_out, and_10_out, and_3_out);
  or or_3 (or_3_out, and_11_out, and_4_out);
  or or_4 (or_4_out, and_12_out, and_5_out);
  or or_5 (or_5_out, and_13_out, and_6_out);
  or or_6 (or_6_out, and_14_out, and_7_out);
  or or_7 (or_7_out, and_15_out, and_8_out);
  LED led_1 (.in(or_7_out));
endmodule

module Stage4_FlipData (
  input  [7:0] in_bit,
  output [7:0] out_bit
);

  not not_1 (out_bit[0], in_bit[0]);
  not not_2 (out_bit[1], in_bit[1]);
  not not_3 (out_bit[2], in_bit[2]);
  not not_4 (out_bit[3], in_bit[3]);
  not not_5 (out_bit[4], in_bit[4]);
  not not_6 (out_bit[5], in_bit[5]);
  not not_7 (out_bit[6], in_bit[6]);
  not not_8 (out_bit[7], in_bit[7]);
endmodule
