// Logisim project q10-11.circ as structural Verilog: 1 circuit, main circuit main
module main (
  input  pin1,
  input  pin2
);

  wire xor_1_out;

  xor xor_1 (xor_1_out, pin1, pin2);
  LED led_1 (.in(xor_1_out));
endmodule
