// Logisim project q12-q14.circ as structural Verilog: 1 circuit, main circuit main
module main (
  input  pin1,
  input  pin2
);

  wire not_1_out, xor_1_out;

  xor xor_1 (xor_1_out, pin1, pin2);
  not not_1 (not_1_out, xor_1_out);
  LED led_1 (.in(not_1_out));
endmodule
