// Logisim project q15.circ as structural Verilog: 1 circuit, main circuit main
module main (
  input  pin1,
  input  pin2,
  input  pin3,
  input  in_4,
  input  in_5
);

  wire and_1_out, not_1_out, not_2_out, not_3_out, xor_1_out, xor_2_out, xor_3_out;

  not not_1 (not_1_out, pin2);
  not not_2 (not_2_out, pin3);
  not not_3 (not_3_out, in_5);
  xor xor_1 (xor_1_out, pin1, not_1_out);
  xor xor_2 (xor_2_out, pin2, not_2_out);
  xor xor_3 (xor_3_out, in_4, not_3_out);
  LED led_1 (.in(xor_3_out));
  and and_1 (and_1_out, xor_1_out, xor_2_out);
  LED led_2 (.in(and_1_out));
endmodule
