// Logisim project q2.circ as structural Verilog: 1 circuit, main circuit main
module main (
  input  Input1,
  input  Input2,
  input  carryin,
  input  pin1,
  input  pin2,
  input  A0,
  input  B0,
  input  A1,
  input  B1,
  input  A2,
  input  B2,
  input  A3,
  input  B3
);

  wire and_1_out, and_2_out, and_3_out, and_4_out, and_5_out, and_6_out, and_7_out, and_8_out, and_9_out,
       Carry_out, or_1_out, or_2_out, or_3_out, or_4_out, Sum_out, xor_1_out, xor_2_out, xor_3_out,
       xor_4_out, xor_5_out, xor_6_out, xor_7_out, xor_8_out, xor_9_out;

  xor xor_1 (xor_1_out, pin1, pin2);
  and and_1 (and_1_out, pin1, pin2);
  xor xor_2 (xor_2_out, A0, B0);
  and and_2 (and_2_out, A0, B0);
  xor xor_3 (xor_3_out, A1, B1);
  and and_3 (and_3_out, A1, B1);
  xor xor_4 (xor_4_out, A2, B2);
  and and_4 (and_4_out, A2, B2);
  xor xor_5 (xor_5_out, A3, B3);
  and and_5 (and_5_out, A3, B3);
  xor Sum (Sum_out, Input1, Input2);
  LED led_1 (.in(Sum_out));
  and Carry (Carry_out, Input1, Input2);
  LED led_2 (.in(Carry_out));
  xor xor_6 (xor_6_out, carryin, xor_1_out);
  and and_6 (and_6_out, carryin, xor_1_out);
  xor xor_7 (xor_7_out, and_2_out, xor_3_out);
  and and_7 (and_7_out, and_2_out, xor_3_out);
  xor xor_8 (xor_8_out, or_2_out, xor_4_out);
  and and_8 (and_8_out, or_2_out, xor_4_out);
  xor xor_9 (xor_9_out, or_3_out, xor_5_out);
  and and_9 (and_9_out, or_3_out, xor_5_out);
  LED led_3 (.in(xor_6_out));
  or or_1 (or_1_out, and_6_out, and_1_out);
  LED led_4 (.in(or_1_out));
  LED led_5 (.in(xor_2_out));
  LED led_6 (.in(xor_7_out));
  or or_2 (or_2_out, and_7_out, and_3_out);
  LED led_7 (.in(xor_8_out));
  or or_3 (or_3_out, and_8_out, and_4_out);
  LED led_8 (.in(xor_9_out));
  or or_4 (or_4_out, and_9_out, and_5_out);
  LED led_9 (.in(or_4_out));
endmodule
