// Logisim project lab03.circ as structural Verilog: 1 circuit, main circuit main
module main (
  input  Set,
  input  Reset,
  input  in_3,
  input  in_4,
  input  in_5,
  input  in_6,
  input  in_7,
  input  in_8,
  input  in_9,
  input  in_10
);

  wire and_1_out, and_2_out, clock_1_out, clock_2_out, clock_3_out, clock_4_out, d_ff_1_q, d_ff_2_q,
       d_ff_3_q, d_ff_4_q, d_ff_5_q, nand_1_out, nand_2_out, nand_3_out, nand_4_out, nor_1_out, nor_2_out,
       nor_3_out, nor_4_out, not_1_out;

  Clock #(.phaseOffset(1)) clock_1 (.out(clock_1_out));
  Clock #(.phaseOffset(1)) clock_2 (.out(clock_2_out));
  D_Flip_Flop d_ff_1 (.D(in_7), .clk(clock_3_out), .Q(d_ff_1_q));  // open: Qn, preset, reset
  Clock #(.phaseOffset(1)) clock_3 (.out(clock_3_out));
  not not_1 (not_1_out, in_3);
  LED led_1 (.in(d_ff_1_q));
  and and_1 (and_1_out, clock_1_out, not_1_out);
  and and_2 (and_2_out, clock_1_out, in_3);
  nand nand_1 (nand_1_out, nand_4_out, clock_2_out);
  nand nand_2 (nand_2_out, clock_2_out, nand_3_out);
  D_Flip_Flop d_ff_2 (.D(in_6), .clk(clock_4_out), .Q(d_ff_2_q));  // open: Qn, preset, reset
  LED led_2 (.in(d_ff_2_q));
  Clock #(.phaseOffset(1)) clock_4 (.out(clock_4_out));
  D_Flip_Flop d_ff_3 (.D(in_8), .clk(clock_3_out), .Q(d_ff_3_q));  // open: Qn, preset, reset
  LED led_3 (.in(d_ff_3_q));
  nor nor_1 (nor_1_out, Set, nor_2_out);
  LED led_4 (.in(nor_1_out));
  nor nor_2 (nor_2_out, nor_1_out, Reset);
  LED led_5 (.in(nor_2_out));
  nor nor_3 (nor_3_out, and_1_out, nor_4_out);
  nor nor_4 (nor_4_out, nor_3_out, and_2_out);
  nand nand_3 (nand_3_out, nand_1_out, nand_4_out);
  nand nand_4 (nand_4_out, nand_3_out, nand_2_out);
  D_Flip_Flop d_ff_4 (.D(in_9), .clk(clock_3_out), .Q(d_ff_4_q));  // open: Qn, preset, reset
  LED led_6 (.in(nor_3_out));
  LED led_7 (.in(nor_4_out));
  LED Q (.in(nand_3_out));
  LED Qd (.in(nand_4_out));
  D_Flip_Flop d_ff_5 (.D(in_10), .clk(clock_3_out), .Q(d_ff_5_q));  // open: Qn, preset, reset
  LED led_8 (.in(d_ff_4_q));
  LED led_9 (.in(d_ff_5_q));
endmodule
