// Logisim project lab04.circ as structural Verilog: 1 circuit, main circuit main
module main (
  input  in_1,
  input  in_2,
  input  in_3,
  input  in_4,
  input  in_5,
  input  in_6
);

  wire and_1_out, and_2_out, and_3_out, and_4_out, and_5_out, clock_1_out, clock_2_out, clock_3_out,
       clock_4_out, clock_5_out, d_ff_1_q, d_ff_3_q, d_ff_5_q, j_k_ff_1_q, j_k_ff_2_q, j_k_ff_3_q,
       j_k_ff_4_q, j_k_ff_5_q, j_k_ff_6_q, j_k_ff_7_q, j_k_ff_8_q, j_k_ff_9_q, j_k_ff_10_q, j_k_ff_11_q,
       j_k_ff_12_q, j_k_ff_13_q, j_k_ff_14_q, j_k_ff_15_q;
  wire [2:0] d_ff_6_q;

  Clock clock_1 (.out(clock_1_out));
  Clock clock_2 (.out(clock_2_out));
  Clock clock_3 (.out(clock_3_out));
  Clock clock_4 (.out(clock_4_out));
  Clock clock_5 (.out(clock_5_out));
  J_K_Flip_Flop #(.trigger("falling")) j_k_ff_1 (
    .J(in_1), .K(in_1), .clk(clock_1_out), .Q(j_k_ff_1_q));  // open: Qn, preset, reset
  J_K_Flip_Flop j_k_ff_2 (.J(in_2), .K(in_2), .clk(clock_2_out), .Q(j_k_ff_2_q));  // open: Qn, preset, reset
  J_K_Flip_Flop #(.trigger("falling")) j_k_ff_3 (
    .J(in_3), .K(in_3), .clk(clock_3_out), .Q(j_k_ff_3_q));  // open: Qn, preset, reset
  J_K_Flip_Flop #(.trigger("falling")) j_k_ff_4 (
    .J(in_4), .K(in_4), .clk(clock_4_out), .Q(j_k_ff_4_q), .reset(and_4_out));  // open: Qn, preset
  J_K_Flip_Flop #(.trigger("falling")) j_k_ff_5 (
    .J(in_5), .K(in_5), .clk(clock_5_out), .Q(j_k_ff_5_q), .reset(and_5_out));  // open: Qn, preset
  J_K_Flip_Flop #(.trigger("falling")) j_k_ff_6 (
    .J(in_1), .K(in_1), .clk(j_k_ff_1_q), .Q(j_k_ff_6_q));  // open: Qn, preset, reset
  LED led_1 (.in(j_k_ff_11_q));
  LED led_2 (.in(j_k_ff_12_q));
  LED led_3 (.in(j_k_ff_13_q));
  LED led_4 (.in(j_k_ff_14_q));
  D_Flip_Flop d_ff_1 (.D(j_k_ff_14_q), .clk(clock_4_out), .Q(d_ff_1_q));  // open: Qn, preset, reset
  LED led_5 (.in(j_k_ff_15_q));
  D_Flip_Flop d_ff_2 (.D(j_k_ff_15_q), .clk(clock_5_out), .Q(d_ff_6_q[2]));  // open: Qn, preset, reset
  LED led_6 (.in(j_k_ff_6_q));
  J_K_Flip_Flop j_k_ff_7 (.J(in_2), .K(in_2), .clk(j_k_ff_2_q), .Q(j_k_ff_7_q));  // open: Qn, preset, reset
  LED led_7 (.in(j_k_ff_7_q));
  J_K_Flip_Flop #(.trigger("falling")) j_k_ff_8 (
    .J(j_k_ff_3_q), .K(j_k_ff_3_q), .clk(clock_3_out), .Q(j_k_ff_8_q));  // open: Qn, preset, reset
  LED led_8 (.in(j_k_ff_8_q));
  J_K_Flip_Flop #(.trigger("falling")) j_k_ff_9 (
    .J(j_k_ff_4_q), .K(j_k_ff_4_q), .clk(clock_4_out), .Q(j_k_ff_9_q), .reset(and_4_out));  // open: Qn, preset
  LED led_9 (.in(j_k_ff_9_q));
  LED led_10 (.in(d_ff_1_q));
  J_K_Flip_Flop #(.trigger("falling")) j_k_ff_10 (
    .J(j_k_ff_5_q), .K(j_k_ff_5_q), .clk(clock_5_out), .Q(j_k_ff_10_q), .reset(and_5_out));  // open: Qn, preset
  LED led_11 (.in(j_k_ff_10_q));
  J_K_Flip_Flop #(.trigger("falling")) j_k_ff_11 (
    .J(in_1), .K(in_1), .clk(j_k_ff_6_q), .Q(j_k_ff_11_q));  // open: Qn, preset, reset
  J_K_Flip_Flop j_k_ff_12 (.J(in_2), .K(in_2), .clk(j_k_ff_7_q), .Q(j_k_ff_12_q));  // open: Qn, preset, reset
  and and_1 (and_1_out, j_k_ff_3_q, j_k_ff_8_q);
  J_K_Flip_Flop #(.trigger("falling")) j_k_ff_13 (
    .J(and_1_out), .K(and_1_out), .clk(clock_3_out), .Q(j_k_ff_13_q));  // open: Qn, preset, reset
  and and_2 (and_2_out, j_k_ff_4_q, j_k_ff_9_q);
  J_K_Flip_Flop #(.trigger("falling")) j_k_ff_14 (
    .J(and_2_out), .K(and_2_out), .clk(clock_4_out), .Q(j_k_ff_14_q), .reset(and_4_out));  // open: Qn, preset
  D_Flip_Flop d_ff_3 (.D(j_k_ff_9_q), .clk(clock_4_out), .Q(d_ff_3_q));  // open: Qn, preset, reset
  and and_3 (and_3_out, j_k_ff_5_q, j_k_ff_10_q);
  J_K_Flip_Flop #(.trigger("falling")) j_k_ff_15 (
    .J(and_3_out), .K(and_3_out), .clk(clock_5_out), .Q(j_k_ff_15_q), .reset(and_5_out));  // open: Qn, preset
  D_Flip_Flop d_ff_4 (.D(j_k_ff_10_q), .clk(clock_5_out), .Q(d_ff_6_q[1]));  // open: Qn, preset, reset
  LED led_12 (.in(j_k_ff_1_q));
  LED led_13 (.in(j_k_ff_2_q));
  LED led_14 (.in(j_k_ff_3_q));
  LED led_15 (.in(j_k_ff_4_q));
  D_Flip_Flop d_ff_5 (.D(j_k_ff_4_q), .clk(clock_4_out), .Q(d_ff_5_q));  // open: Qn, preset, reset
  LED led_16 (.in(d_ff_3_q));
  LED led_17 (.in(j_k_ff_5_q));
  D_Flip_Flop d_ff_6 (.D(j_k_ff_5_q), .clk(clock_5_out), .Q(d_ff_6_q[0]));  // open: Qn, preset, reset
  and and_4 (and_4_out, j_k_ff_14_q, j_k_ff_9_q);
  LED led_18 (.in(d_ff_5_q));
  and and_5 (and_5_out, j_k_ff_15_q, j_k_ff_10_q);
  Hex_Digit_Display hex_digit_display_1 (.value({in_6, d_ff_6_q}));  // open: dp
endmodule
